# Fritzing sketch ZillerSafetyMonitor (saved by Fritzing 1.0.5)
circuit board: 8.46667cm x 5.64444cm
breadboards: 1

parts:
  ESP8266 = Amica NodeMCU DEVKIT 1.0
  U1 = MLX90614 [package=to-39]
  RHT1 = Humidity and Temperature Sensor RHT03
  BMP260 = Barometric Pressure Sensor - BMP180 Breakout (GY-68)
  R1 = Resistor [tolerance=±5% power=0.25W resistance=10k package=THT]

nets:
  VCC: ESP8266.pin1, ESP8266.pin_10, ESP8266.pin_26, U1.VDD, RHT1.Vcc, BMP260.VCC, R1.Pin_1
  VSS: ESP8266.pin2, ESP8266.pin_9, ESP8266.pin_25, ESP8266.pin_29, U1.VSS, RHT1.GND_2, BMP260.GND
  N1: ESP8266.pin_12, RHT1.Data-signal, R1.Pin_0
  N2: ESP8266.pin_13, U1.PWM_SDA, BMP260.SDA
  N3: ESP8266.pin_14, U1.SCL_VZ, BMP260.SCL

notes:
  To rain sensor
